# Fritzing sketch Buch (saved by Fritzing 0.9.3b)

parts:
  Seite02-Klopfpuzzle = mystery part, 2 pins [chip_label="Arduino + E. Magnet"]
  Seite03-Farbkreispuzzle = mystery part, 2 pins [chip_label="Arduino + E. Magnet"]
  Seite04-Endoskoppuzzle = mystery part, 2 pins [chip_label="Arduino + E. Magnet"]
  Seite05-Menschenkette = mystery part, 2 pins [chip_label="Arduino + E. Magnet"]
  Seite06-Steckpuzzle = mystery part, 2 pins [chip_label="Arduino + E. Magnet"]
  Seite07-Melodiepuzzle = mystery part, 3 pins [chip_label="Arduino + E. Magnet"]
  Seite08-RFID-Finalstein = mystery part, 3 pins [chip_label=Arduino]
  Seite01-Finale = mystery part, 4 pins [chip_label="Arduino + Lautsprecher"]
  Seite01-RFID-Edelsteinpuzzle = mystery part, 3 pins [chip_label=Arduino]

nets:
  12V: Seite02-Klopfpuzzle.pin1, Seite03-Farbkreispuzzle.pin1, Seite04-Endoskoppuzzle.pin1, Seite05-Menschenkette.pin1, Seite06-Steckpuzzle.pin1, Seite07-Melodiepuzzle.pin1, Seite08-RFID-Finalstein.pin1, Seite01-Finale.pin1, Seite01-RFID-Edelsteinpuzzle.pin1
  GND: Seite02-Klopfpuzzle.pin2, Seite03-Farbkreispuzzle.pin2, Seite04-Endoskoppuzzle.pin2, Seite05-Menschenkette.pin2, Seite06-Steckpuzzle.pin2, Seite07-Melodiepuzzle.pin2, Seite08-RFID-Finalstein.pin2, Seite01-Finale.pin2, Seite01-RFID-Edelsteinpuzzle.pin2
  N1: Seite07-Melodiepuzzle.pin3, Seite01-Finale.pin3, Seite01-RFID-Edelsteinpuzzle.pin3
  N2: Seite08-RFID-Finalstein.pin3, Seite01-Finale.pin4
