# Fritzing sketch Finale (saved by Fritzing 0.9.3b)

parts:
  Arduino = Arduino Uno (Rev3)
  R7 = Resistor [tolerance=±5% resistance=1k package=THT]
  R8 = Resistor [tolerance=±5% resistance=1k package=THT]
  C1 = Ceramic Capacitor [capacitance=10µF package="100 mil [THT, multilayer]"]
  R9 = Resistor [tolerance=±5% resistance=100k package=THT]
  RFID_Steinerkennung_Pentagramm = mystery part, 2 pins [chip_label=?]
  R10 = Resistor [tolerance=±5% resistance=1k package=THT]
  R11 = Resistor [tolerance=±5% resistance=1k package=THT]
  C2 = Ceramic Capacitor [capacitance=10µF package="100 mil [THT, multilayer]"]
  R12 = Resistor [tolerance=±5% resistance=100k package=THT]
  RFID_Steinerkennung_Melodiestein = mystery part, 2 pins [chip_label=?]
  4_digit_7_segment_display = mystery part, 4 pins [chip_label=Serial]
  microSD1 = MicroSD Card Module
  SPKR1 = Loudspeaker

nets:
  N1: Arduino.D9_PWM, SPKR1.pin1
  N2: Arduino.D10_PWM/SS, microSD1.CS
  N3: Arduino.D11_PWM/MOSI, microSD1.MOSI
  N4: Arduino.D12/MISO, microSD1.MISO
  N5: Arduino.D13/SCK, microSD1.SCK
  GND: Arduino.GND, R7.Pin_0, C1.1, R9.Pin_1, R11.Pin_0, C2.1, R12.Pin_1, 4_digit_7_segment_display.pin4, microSD1.GND, SPKR1.pin2
  N6: Arduino.D2, 4_digit_7_segment_display.pin2
  N7: Arduino.D3_PWM, 4_digit_7_segment_display.pin1
  N8: Arduino.D4, R8.Pin_0, C1.0, R9.Pin_0
  N9: Arduino.D6_PWM, R10.Pin_0, C2.0, R12.Pin_0
  5V: Arduino.5V, 4_digit_7_segment_display.pin3, microSD1.VCC
  12V: Arduino.VIN
  N10: R7.Pin_1, RFID_Steinerkennung_Pentagramm.pin2
  N11: R8.Pin_1, RFID_Steinerkennung_Pentagramm.pin1
  N12: R10.Pin_1, RFID_Steinerkennung_Melodiestein.pin1
  N13: R11.Pin_1, RFID_Steinerkennung_Melodiestein.pin2
