# Fritzing sketch Farbkreispuzzle (saved by Fritzing 0.9.3b)

parts:
  Arduino = Arduino Uno (Rev3)
  Lichtsensor_Iduino_SE012 = mystery part, 3 pins
  Lichtsensor_Iduino_SE13 = mystery part, 3 pins [chip_label=?]
  Lichtsensor_Iduino_SE14 = mystery part, 3 pins [chip_label=?]
  SUMMER = Piezo Speaker
  Elektromagnet = mystery part, 2 pins [chip_label=?]
  Relais = mystery part, 6 pins

nets:
  N1: Arduino.A2, Lichtsensor_Iduino_SE012.pin1
  N2: Arduino.A3, Lichtsensor_Iduino_SE13.pin1
  N3: Arduino.D10_PWM/SS, Relais.pin3
  GND: Arduino.GND, Lichtsensor_Iduino_SE012.pin3, Lichtsensor_Iduino_SE13.pin3, Lichtsensor_Iduino_SE14.pin3, SUMMER.pin2, Elektromagnet.pin2, Relais.pin4
  N4: Arduino.A4/SDA, Lichtsensor_Iduino_SE14.pin1
  N5: Arduino.D2, SUMMER.pin1
  N6: Arduino.5V, Lichtsensor_Iduino_SE012.pin2, Lichtsensor_Iduino_SE13.pin2, Lichtsensor_Iduino_SE14.pin2
  12V: Arduino.VIN, Relais.pin1
  N7: Elektromagnet.pin1, Relais.pin6
