# Fritzing sketch Endoskoppuzzle (saved by Fritzing 0.9.3b)

parts:
  Arduino = Arduino Uno (Rev3)
  Elektromagnet = mystery part, 2 pins [chip_label=?]
  Relais = mystery part, 6 pins [chip_label=?]
  Arduino_Keypad_Matrix_3x4 = mystery part, 7 pins

nets:
  N1: Arduino.D8, Arduino_Keypad_Matrix_3x4.pin7
  N2: Arduino.D10_PWM/SS, Relais.pin3
  GND: Arduino.GND, Elektromagnet.pin2, Relais.pin4
  N3: Arduino.D2, Arduino_Keypad_Matrix_3x4.pin1
  N4: Arduino.D3_PWM, Arduino_Keypad_Matrix_3x4.pin2
  N5: Arduino.D4, Arduino_Keypad_Matrix_3x4.pin3
  N6: Arduino.D5_PWM, Arduino_Keypad_Matrix_3x4.pin4
  N7: Arduino.D6_PWM, Arduino_Keypad_Matrix_3x4.pin5
  N8: Arduino.D7, Arduino_Keypad_Matrix_3x4.pin6
  N9: Arduino.5V, Relais.pin2
  12V: Arduino.VIN, Relais.pin1
  N10: Elektromagnet.pin1, Relais.pin6
