# Fritzing sketch Steckpuzzle (saved by Fritzing 0.9.3b)

parts:
  Arduino = Arduino Uno (Rev3)
  Elektromagnet = mystery part, 2 pins [chip_label=?]
  Relais = mystery part, 6 pins [chip_label=?]
  R1 = Resistor [tolerance=±1% resistance=1.2k package=THT]
  R2 = Resistor [tolerance=±1% resistance=1.2k package=THT]
  R3 = Resistor [tolerance=±1% resistance=1.2k package=THT]
  R4 = Resistor [tolerance=±1% resistance=1.2k package=THT]
  R5 = Resistor [tolerance=±1% resistance=1.2k package=THT]
  R6 = Resistor [tolerance=±1% resistance=1.2k package=THT]
  R7 = Resistor [tolerance=±1% resistance=1.2k package=THT]
  R8 = Resistor [tolerance=±1% resistance=1.2k package=THT]
  R9 = Resistor [tolerance=±1% resistance=1.2k package=THT]
  R10 = Resistor [tolerance=±1% resistance=1.2k package=THT]
  Stecker1 = single row smd female pin header, 1 pin [form="♀ (female)"]
  Stecker2 = single row smd female pin header, 1 pin [form="♀ (female)"]
  Stecker3 = single row smd female pin header, 1 pin [form="♀ (female)"]
  Stecker4 = single row smd female pin header, 1 pin [form="♀ (female)"]
  Stecker5 = single row smd female pin header, 1 pin [form="♀ (female)"]
  SteckerA = female pin header, 1 pin [form="♀ (female)"]
  SteckerB = female pin header, 1 pin [form="♀ (female)"]
  SteckerC = female pin header, 1 pin [form="♀ (female)"]
  SteckerD = female pin header, 1 pin [form="♀ (female)"]
  SteckerE = female pin header, 1 pin [form="♀ (female)"]

nets:
  N1: Arduino.A0, R1.Pin_1
  N2: Arduino.A1, R2.Pin_1
  N3: Arduino.A2, R3.Pin_1
  N4: Arduino.A3, R4.Pin_1
  N5: Arduino.A5/SCL, Relais.pin3
  N6: Arduino.D9_PWM, R8.Pin_0
  N7: Arduino.D10_PWM/SS, R7.Pin_0
  GND: Arduino.GND, Elektromagnet.pin2, Relais.pin4
  N8: Arduino.A4/SDA, R5.Pin_1
  N9: Arduino.D3_PWM, R6.Pin_0
  N10: Arduino.D5_PWM, R9.Pin_0
  N11: Arduino.D6_PWM, R10.Pin_0
  N12: Arduino.5V, Relais.pin2
  12V: Arduino.VIN, Relais.pin1
  N13: Elektromagnet.pin1, Relais.pin6
  N14: R1.Pin_0, Stecker1.pin1
  N15: R2.Pin_0, Stecker2.pin1
  N16: R3.Pin_0, Stecker3.pin1
  N17: R4.Pin_0, Stecker4.pin1
  N18: R5.Pin_0, Stecker5.pin1
  N19: R6.Pin_1, SteckerA.pin1
  N20: R7.Pin_1, SteckerE.pin1
  N21: R8.Pin_1, SteckerD.pin1
  N22: R9.Pin_1, SteckerB.pin1
  N23: R10.Pin_1, SteckerC.pin1
