# Fritzing sketch Melodiepuzzle (saved by Fritzing 0.9.3b)

parts:
  Arduino = Arduino Uno (Rev3)
  Elektromagnet = mystery part, 2 pins [chip_label=?]
  Relais = mystery part, 6 pins [chip_label=?]
  LED1 = RGB LED (com. cathode, rbg) [package="5 mm [THT]"]
  LED2 = RGB LED (com. cathode, rbg) [package="5 mm [THT]"]
  R1 = Resistor [tolerance=±5% resistance=100 package=THT]
  R2 = Resistor [tolerance=±5% resistance=100 package=THT]
  R3 = Resistor [tolerance=±5% resistance=100 package=THT]
  R4 = Resistor [tolerance=±5% resistance=100 package=THT]
  R5 = Resistor [tolerance=±5% resistance=150 package=THT]
  R6 = Resistor [tolerance=±5% resistance=150 package=THT]
  Button1 = Pushbutton [package=THT]
  Button2 = Pushbutton [package=THT]
  Button3 = Pushbutton [package=THT]
  Button4 = Pushbutton [package=THT]
  SPKR1 = Loudspeaker
  R7 = Resistor [tolerance=±5% resistance=1k package=THT]
  R8 = Resistor [tolerance=±5% resistance=1k package=THT]
  C1 = Ceramic Capacitor [capacitance=10µF package="100 mil [THT, multilayer]"]
  R9 = Resistor [tolerance=±5% resistance=100k package=THT]
  RFID_Steinerkennung = mystery part, 2 pins [chip_label=?]

nets:
  N1: Arduino.A0, R6.Pin_1
  N2: Arduino.A1, R1.Pin_1
  N3: Arduino.A2, R2.Pin_1
  N4: Arduino.A3, R4.Pin_1
  N5: Arduino.D8, SPKR1.pin1
  N6: Arduino.D10_PWM/SS, Button1.leg0
  N7: Arduino.D11_PWM/MOSI, Button2.leg0
  N8: Arduino.D12/MISO, Button3.leg0
  N9: Arduino.D13/SCK, Button4.leg0
  GND: Arduino.GND, Elektromagnet.pin2, Relais.pin4, LED1.common_cathode, LED2.common_cathode, Button1.leg1, Button2.leg1, Button3.leg1, Button4.leg1, SPKR1.pin2
  N10: Arduino.A4/SDA, R3.Pin_1
  N11: Arduino.A5/SCL, R5.Pin_1
  N12: Arduino.D4, R8.Pin_0, C1.0, R9.Pin_0
  N13: Arduino.D6_PWM, Relais.pin3
  N14: Arduino.5V, Relais.pin2
  12V: Arduino.VIN, Relais.pin1
  N15: Elektromagnet.pin1, Relais.pin6
  N16: LED1.red_anode, R6.Pin_0
  N17: LED1.blue_anode, R2.Pin_0
  N18: LED1.green_anode, R1.Pin_0
  N19: LED2.red_anode, R5.Pin_0
  N20: LED2.blue_anode, R4.Pin_0
  N21: LED2.green_anode, R3.Pin_0
  N22: R7.Pin_0, C1.1, R9.Pin_1
  N23: R7.Pin_1, RFID_Steinerkennung.pin2
  N24: R8.Pin_1, RFID_Steinerkennung.pin1
