# Fritzing sketch ReadAndWriteLastStone (saved by Fritzing 0.9.3b)

parts:
  Arduino = Arduino Uno (Rev3)
  Finale = mystery part, 2 pins [chip_label=?]
  RFID_Reader = mystery part, 7 pins [chip_label=?]

nets:
  N1: Arduino.D9_PWM, RFID_Reader.pin2
  N2: Arduino.D10_PWM/SS, RFID_Reader.pin3
  N3: Arduino.D11_PWM/MOSI, RFID_Reader.pin4
  N4: Arduino.D12/MISO, RFID_Reader.pin5
  N5: Arduino.D13/SCK, RFID_Reader.pin6
  GND: Arduino.GND, Finale.pin2, RFID_Reader.pin7
  N6: Arduino.D5_PWM, Finale.pin1
  N7: Arduino.3V3, RFID_Reader.pin1
  12V: Arduino.VIN
